// Digital circuit digitalfile.dig as structural Verilog
module digitalfile (
  input  [7:0] M,
  input  [7:0] N,
  input  [13:0] progIn,
  input  reset,
  input  progLoad,
  input  start,
  input  result,
  input  clk,
  output [7:0] out_9,
  output [7:0] out_10,
  output [7:0] out_11,
  output [7:0] out_12,
  output [5:0] Instruction,
  output valid,
  output done,
  output [7:0] \output ,
  output [5:0] instruction_2,
  output [13:0] out_18,
  output [7:0] Z,
  output [1:0] out_20,
  output [7:0] out_21,
  output [7:0] out_22,
  output out_23
);

  wire _110000eq, _110000gt, _110000ls, _110001eq, _110010eq, accAen, accBen, accCen, accDen, and_1_out,
       and_2_out, and_3_out, and_7_out, and_8_out, and_9_out, and_10_out, and_11_out, and_12_out, and_13_out,
       and_19_out, and_20_out, and_21_out, cd_to_ab, cmp, comparator_2_eq, comparator_3_eq, condition,
       division, eq, gt, Jump_Op_d, mn_to_cd, nand_1_out, nand_2_out, nand_3_out, not_1_out, not_2_out,
       not_4_out, or_1_out, or_2_out, or_3_out, or_4_out, or_5_out, or_6_out, or_7_out, or_8_out, or_10_out,
       or_11_out, prime, Q, ready, reset_Out, result_Out, rRAMen;
  wire [2:0] en;
  wire [7:0] _32, _33, _34, _35, _36, _37, _40, _41, _42, _43, _44, _45, _46, _47, add_2_s, cache,
       counter_2_out, counter_3_out, data, div_3_r, multiplexer_1_out, multiplexer_2_out, multiplexer_3_out,
       multiplexer_4_out, multiplexer_8_out, multiplexer_9_out, multiplexer_10_out, multiplexer_11_out,
       rAddress, rpRAM, rrRAM;
  wire [13:0] d_ff_1_q, pRAM_d2;
  wire [13:8] pRAM_d1;

  not not_1 (not_1_out, clk);
  not not_2 (not_2_out, clk);
  Register #(.Bits(8)) u_cache (.D(data), .C(not_1_out), .en(1'b1), .Q(cache));
  Register #(.Bits(3)) write_remem (.D(en), .C(not_2_out), .en(1'b1));  // open: Q
  and and_1 (and_1_out, _110010eq, division);
  Multiplexer #(.Bits(8)) multiplexer_1 (.sel(cd_to_ab), .in_0(data), .in_1(out_11), .out(multiplexer_1_out));
  or or_1 (or_1_out, reset, cd_to_ab, accAen);
  Multiplexer #(.Bits(8)) multiplexer_2 (.sel(cd_to_ab), .in_0(data), .in_1(out_12), .out(multiplexer_2_out));
  or or_2 (or_2_out, reset, cd_to_ab, accBen);
  Multiplexer #(.Bits(8)) multiplexer_3 (.sel(mn_to_cd), .in_0(data), .in_1(M), .out(multiplexer_3_out));
  or or_3 (or_3_out, reset, mn_to_cd, accCen);
  Multiplexer #(.Bits(8)) multiplexer_4 (.sel(mn_to_cd), .in_0(data), .in_1(N), .out(multiplexer_4_out));
  or or_4 (or_4_out, reset, mn_to_cd, accDen);
  Register #(.Bits(8)) register_1 (.D(multiplexer_1_out), .C(clk), .en(or_1_out), .Q(out_9));
  Register #(.Bits(8)) register_2 (.D(multiplexer_3_out), .C(clk), .en(or_3_out), .Q(out_11));
  and and_2 (and_2_out, _110001eq, prime);
  and and_3 (and_3_out, _110000eq, cmp);
  and and_4 (cmp, ~Instruction[0], ~Instruction[1], ~Instruction[2], ~Instruction[3], Instruction[4], Instruction[5]);  // And
  and and_5 (prime, Instruction[0], ~Instruction[1], ~Instruction[2], ~Instruction[3], Instruction[4], Instruction[5]);  // And
  and and_6 (division, ~Instruction[0], Instruction[1], ~Instruction[2], ~Instruction[3], Instruction[4], Instruction[5]);  // And
  LED u_Start (.in(Q));
  and and_7 (and_7_out, ~Instruction[0], ~Instruction[1], ~Instruction[2], ~Instruction[3], ~Instruction[4], ~Instruction[5]);  // And
  Register #(.Bits(8)) register_3 (.D(multiplexer_2_out), .C(clk), .en(or_2_out), .Q(out_10));
  Register #(.Bits(8)) register_4 (.D(multiplexer_4_out), .C(clk), .en(or_4_out), .Q(out_12));
  and and_8 (and_8_out, ~ready, reset, ~reset_Out);  // And
  and and_9 (and_9_out, ready, reset_Out);
  and and_10 (and_10_out, ~reset, result, ~result_Out);  // And
  and and_11 (and_11_out, reset, result_Out);
  and and_12 (and_12_out, ~reset, start, ~Q);  // And
  and and_13 (and_13_out, reset, Q);
  LED Idle (.in(and_7_out));
  or or_5 (or_5_out, and_2_out, and_1_out, and_3_out);
  or or_6 (or_6_out, division, cmp, prime);
  nand nand_1 (nand_1_out, ~and_8_out, ~and_9_out);  // NAnd
  nand nand_2 (nand_2_out, ~and_10_out, ~and_11_out);  // NAnd
  nand nand_3 (nand_3_out, ~and_12_out, ~and_13_out);  // NAnd
  LED u_Reset (.in(reset_Out));
  LED u_Result (.in(result_Out));
  and and_14 (mn_to_cd, Instruction[0], ~Instruction[1], Instruction[2], Instruction[3], ~Instruction[4], ~Instruction[5]);  // And
  and and_15 (cd_to_ab, ~Instruction[0], Instruction[1], Instruction[2], Instruction[3], ~Instruction[4], ~Instruction[5]);  // And
  Register equal_flag (.D(or_5_out), .C(clk), .en(or_6_out), .Q(eq));
  Register greater_flag (.D(_110000gt), .C(clk), .en(cmp), .Q(gt));
  Register lesser_flag (.D(_110000ls), .C(clk), .en(cmp), .Q(out_23));
  T_FF t_ff_1 (.T(nand_1_out), .C(clk), .Q(reset_Out));  // open: nQ
  T_FF t_ff_2 (.T(nand_2_out), .C(clk), .Q(result_Out));  // open: nQ
  T_FF t_ff_3 (.T(nand_3_out), .C(clk), .Q(Q));  // open: nQ
  Multiplexer #(.Selector_Bits(6), .Bits(8)) multiplexer_5 (
    .sel(Instruction), .in_0({8{1'b0}}), .in_1(out_18[7:0]), .in_2(out_18[7:0]), .in_3(out_10), .in_4(out_9),
    .in_5(out_9), .in_6(out_11), .in_7(out_9), .in_8(out_12), .in_9(M), .in_10(N), .in_11(M), .in_12(N),
    .in_13(M), .in_14(out_11), .in_15(rpRAM), .in_16(rrRAM), .in_17(out_9), .in_18(out_18[7:0]),
    .in_19(out_18[7:0]), .in_20(out_18[7:0]), .in_21(out_18[7:0]), .in_22(out_18[7:0]), .in_23(out_18[7:0]),
    .in_24({8{1'b0}}), .in_25({8{1'b0}}), .in_26({8{1'b0}}), .in_27({8{1'b0}}), .in_28({8{1'b0}}),
    .in_29({8{1'b0}}), .in_30({8{1'b0}}), .in_31({8{1'b0}}), .in_32(_32), .in_33(_33), .in_34(_34),
    .in_35(_35), .in_36(_36), .in_37(_37), .in_38({8{1'b0}}), .in_39({8{1'b0}}), .in_40(_40), .in_41(_41),
    .in_42(_42), .in_43(_43), .in_44(_44), .in_45(_45), .in_46(_46), .in_47(_47), .in_48(8'h8), .in_49(8'h6),
    .in_50(8'h6), .in_51({8{1'b0}}), .in_52({8{1'b0}}), .in_53({8{1'b0}}), .in_54({8{1'b0}}),
    .in_55({8{1'b0}}), .in_56({8{1'b0}}), .in_57({8{1'b0}}), .in_58({8{1'b0}}), .in_59({8{1'b0}}),
    .in_60({8{1'b0}}), .in_61({8{1'b0}}), .in_62({8{1'b0}}), .in_63({8{1'b0}}), .out(data));
  Add #(.Bits(8)) add_1 (.a(out_9), .b(out_10), .c_i(1'b0), .s(_32));  // open: c_o
  Sub #(.Bits(8)) sub_1 (.a(out_9), .b(out_10), .c_i(1'b0), .s(_33));  // open: c_o
  Mul #(.Bits(4)) mul_1 (.a(out_9[3:0]), .b(out_10[3:0]), .mul(_34));
  Comparator #(.Signed("true"), .Bits(8)) comparator_1 (
    .a(out_9), .b(out_10), .gt(_110000gt), .eq(_110000eq), .lt(_110000ls));
  BarrelShifter #(.Bits(8)) barrelshifter_1 (.in(out_9), .shift({1'b0, out_10[2:0]}), .out(_44));
  Div #(.Bits(8)) div_1 (.a(out_9), .b(out_10), .q(_35));  // open: r
  Div #(.Bits(8)) div_2 (.a(out_9), .b(out_10), .r(_36));  // open: q
  or or_7 (or_7_out, eq, gt);
  or or_8 (or_8_out, eq, out_23);
  Div #(.Bits(8)) div_3 (.a(out_9), .b(out_10), .r(div_3_r));  // open: q
  Multiplexer #(.Selector_Bits(6)) multiplexer_6 (
    .sel(Instruction), .in_0(1'b1), .in_1(1'b0), .in_2(1'b0), .in_3(1'b0), .in_4(1'b0), .in_5(1'b0),
    .in_6(1'b0), .in_7(1'b0), .in_8(1'b0), .in_9(1'b0), .in_10(1'b0), .in_11(1'b0), .in_12(1'b0),
    .in_13(1'b0), .in_14(1'b0), .in_15(1'b0), .in_16(1'b0), .in_17(1'b0), .in_18(1'b1), .in_19(eq),
    .in_20(gt), .in_21(out_23), .in_22(or_7_out), .in_23(or_8_out), .in_24(1'b0), .in_25(1'b0), .in_26(1'b0),
    .in_27(1'b0), .in_28(1'b0), .in_29(1'b0), .in_30(1'b0), .in_31(1'b0), .in_32(1'b0), .in_33(1'b0),
    .in_34(1'b0), .in_35(1'b0), .in_36(1'b0), .in_37(1'b0), .in_38(1'b0), .in_39(1'b0), .in_40(1'b0),
    .in_41(1'b0), .in_42(1'b0), .in_43(1'b0), .in_44(1'b0), .in_45(1'b0), .in_46(1'b0), .in_47(1'b0),
    .in_48(1'b0), .in_49(1'b0), .in_50(1'b0), .in_51(1'b0), .in_52(1'b0), .in_53(1'b0), .in_54(1'b0),
    .in_55(1'b0), .in_56(1'b0), .in_57(1'b0), .in_58(1'b0), .in_59(1'b0), .in_60(1'b0), .in_61(1'b0),
    .in_62(1'b0), .in_63(1'b0), .out(condition));
  ROM #(.AddrBits(6), .Bits(8)) rom_1 (.A({out_10[2:0], out_9[2:0]}), .sel(1'b1), .D(_37));
  Comparator #(.Bits(6)) comparator_2 (.a(Instruction), .b(6'b110010), .eq(comparator_2_eq));  // open: gt, lt
  Comparator #(.Bits(8)) comparator_3 (.a(div_3_r), .b({8{1'b0}}), .eq(comparator_3_eq));  // open: gt, lt
  ROM #(.AddrBits(6)) Jump_Op (.A(Instruction), .sel(1'b1), .D(Jump_Op_d));
  and and_16 (_110010eq, comparator_2_eq, comparator_3_eq);
  BarrelShifter #(.Bits(8), .barrelShifterMode("rotate")) barrelshifter_2 (
    .in(out_9), .shift({1'b0, out_10[2:0]}), .out(_45));
  and and_17 (out_20[0], condition, Jump_Op_d);
  assign _40 = ~out_9;  // Not not_3, 8 bits wide
  assign _41 = out_9 & out_10;  // And and_18, 8 bits wide
  assign _42 = out_9 | out_10;  // Or or_9, 8 bits wide
  assign _43 = out_9 ^ out_10;  // XOr xor_1, 8 bits wide
  ROM #(.AddrBits(8)) rom_2 (.A(out_9), .sel(1'b1), .D(_110001eq));
  BarrelShifter #(.Bits(8), .direction("right")) barrelshifter_3 (.in(out_9), .shift({1'b0, out_10[2:0]}), .out(_46));
  Multiplexer #(.Selector_Bits(6), .Bits(3)) multiplexer_7 (
    .sel(Instruction), .in_0(3'b101), .in_1(3'b001), .in_2(3'b010), .in_3(3'b001), .in_4(3'b010),
    .in_5(3'b011), .in_6(3'b001), .in_7(3'b100), .in_8(3'b001), .in_9(3'b011), .in_10(3'b011),
    .in_11(3'b100), .in_12(3'b100), .in_13(3'b000), .in_14(3'b000), .in_15(3'b001), .in_16(3'b001),
    .in_17(3'b101), .in_18(3'b110), .in_19(3'b110), .in_20(3'b110), .in_21(3'b110), .in_22(3'b110),
    .in_23(3'b110), .in_24(3'b000), .in_25(3'b000), .in_26(3'b000), .in_27(3'b000), .in_28(3'b000),
    .in_29(3'b000), .in_30(3'b000), .in_31(3'b000), .in_32(3'b001), .in_33(3'b001), .in_34(3'b001),
    .in_35(3'b001), .in_36(3'b001), .in_37(3'b001), .in_38(3'b000), .in_39(3'b000), .in_40(3'b001),
    .in_41(3'b001), .in_42(3'b001), .in_43(3'b001), .in_44(3'b001), .in_45(3'b001), .in_46(3'b001),
    .in_47(3'b001), .in_48(3'b110), .in_49(3'b110), .in_50(3'b110), .in_51(3'b000), .in_52(3'b000),
    .in_53(3'b000), .in_54(3'b000), .in_55(3'b000), .in_56(3'b000), .in_57(3'b000), .in_58(3'b000),
    .in_59(3'b000), .in_60(3'b000), .in_61(3'b000), .in_62(3'b000), .in_63(3'b000), .out(en));
  Decoder #(.Selector_Bits(3)) decoder_1 (
    .sel(en), .out_1(accAen), .out_2(accBen), .out_3(accCen), .out_4(accDen), .out_5(rRAMen));  // open: out_0, out_6, out_7
  BarrelShifter #(.Bits(8), .barrelShifterMode("rotate"), .direction("right")) barrelshifter_4 (
    .in(out_9), .shift({1'b0, out_10[2:0]}), .out(_47));
  not not_4 (not_4_out, progLoad);
  Counter #(.Bits(8)) counter_1 (.en(reset_Out), .C(clk), .clr(ready), .out(rAddress));  // open: ovf
  and and_19 (and_19_out, result_Out, ~done, valid);  // And
  or or_10 (or_10_out, start, reset, result, progLoad);
  and and_20 (and_20_out, Instruction[0], Instruction[1], Instruction[2], Instruction[3], ~Instruction[4], ~Instruction[5]);  // And
  Counter #(.Bits(8)) counter_2 (.en(progLoad), .C(clk), .clr(not_4_out), .out(counter_2_out));  // open: ovf
  Multiplexer #(.Selector_Bits(2), .Bits(8)) multiplexer_8 (
    .sel({reset, out_20[0]}), .in_0(add_2_s), .in_1(out_18[7:0]), .in_2({8{1'b0}}), .in_3({8{1'b0}}),
    .out(multiplexer_8_out));
  Counter #(.Bits(8)) counter_3 (
    .en(and_19_out), .C(clk), .clr(or_10_out), .out({counter_3_out[7:5], done, counter_3_out[3:0]}));  // open: ovf
  D_FF #(.Bits(14)) d_ff_1 (.D(progIn), .C(~clk), .Q(d_ff_1_q));  // open: nQ
  Comparator #(.Bits(8)) comparator_4 (.a(rAddress), .b(8'h10), .eq(ready));  // open: gt, lt
  Multiplexer #(.Bits(8)) multiplexer_9 (.sel(reset_Out), .in_0(out_18[7:0]), .in_1(rAddress), .out(multiplexer_9_out));
  Multiplexer #(.Bits(8)) multiplexer_10 (
    .sel(and_20_out), .in_0(counter_2_out), .in_1(out_18[7:0]), .out(multiplexer_10_out));
  and and_21 (and_21_out, ~valid, clk, Q);  // And
  or or_11 (or_11_out, rRAMen, reset_Out);
  Multiplexer #(.Bits(8)) multiplexer_11 (.sel(reset_Out), .in_0(data), .in_1({8{1'b0}}), .out(multiplexer_11_out));
  D_FF #(.Bits(8)) pc (.D(multiplexer_8_out), .C(and_21_out), .Q(Z));  // open: nQ
  RAMDualAccess #(.AddrBits(8), .Bits(8)) rRAM (
    .str(or_11_out), .C(clk), .ld(1'b1), .A1(multiplexer_9_out), .Din1(multiplexer_11_out),
    .A2({counter_3_out[7:5], done, counter_3_out[3:0]}), .D1(rrRAM), .D2(\output ));
  RAMDualAccess #(.AddrBits(8), .Bits(14)) pRAM (
    .str(progLoad), .C(clk), .ld(and_20_out), .A1(multiplexer_10_out), .Din1(d_ff_1_q), .A2(Z),
    .D1({pRAM_d1, rpRAM}), .D2(pRAM_d2));
  and and_22 (valid, Instruction[0], Instruction[1], Instruction[2], Instruction[3], Instruction[4], Instruction[5]);
  Add #(.Bits(8)) add_2 (.a(Z), .b(8'h1), .c_i(1'b0), .s(add_2_s));  // open: c_o
  Multiplexer #(.Bits(14)) multiplexer_12 (
    .sel(reset), .in_0(pRAM_d2), .in_1({14{1'b0}}), .out({Instruction, out_18[7:0]}));
  // Probe on out_18[7:0]
  Seven_Seg_Hex seven_seg_hex_1 (.d(\output [7:4]), .dp(1'b0));
  Seven_Seg_Hex seven_seg_hex_2 (.d(\output [3:0]), .dp(1'b0));

  assign instruction_2 = Instruction;
  assign out_18[13:8] = Instruction;
  assign out_20[1] = reset;
  assign out_21 = out_10;
  assign out_22 = out_9;

  // Other names for the same wires on the sheet: st = done; accA[7:0] = out_9; accB[7:0] = out_10; halt = valid;
  //   jump = out_20[0]; ls = out_23; operand[7:0] = out_18[7:0]; opCode[5:0] = Instruction; pc[7:0] = Z;
  //   regC[7:0] = out_11; regD[7:0] = out_12

  // Notes on the sheet:
  //   Cache
  //   input
  //   register
  //   flag
  //   State
  //   acc A
  //   reg C
  //   acc B
  //   reg D
  //   ALU
  //   opcode
  //   future1
  //   future2
  //   100000(+)
  //   100001(-)
  //   100010(*)
  //   110000(cmp)
  //   101100(shift left)
  //   100011(/)
  //   100100(%)
  //   jump
  //   100101(pow)
  //   110010(divisible)
  //   101101(rotate left)
  //   contents of rom_1 (hex, n*v repeats v):
  //   0,7*1,0,1,2,3,4,5,6,7,0,1,4,9,10,19,24,31,0,1,8,1b,40,7d,d8,157
  //   ,0,1,10,51,100,41,510,961,0,1,20,f3,400,c35,1e60,41a7,0,1,40,2d9
  //   ,1000,3d09,b640,44f1,0,1,80,88b,4000,1312d,44580,c90f7
  //   contents of Jump_Op (hex, n*v repeats v):
  //   18*0,6*1
  //   101000(NOT)
  //   101001(AND)
  //   101010(OR)
  //   101011(XOR)
  //   110001(prime)
  //   101110(shift right)
  //   en write
  //   contents of rom_2 (hex, n*v repeats v):
  //   0,0,1,1,0,1,0,1,0,0,0,1,0,1,0,0,0,1,0,1,0,0,0,1,5*0,1,0,1,5*0
  //   ,1,0,0,0,1,0,1,0,0,0,1,5*0,1,5*0,1,0,1,5*0,1,0,0,0,1,0,1,5*0,1
  //   ,0,0,0,1,5*0,1,7*0,1,0,0,0,1,0,1,0,0,0,1,0,1,0,0,0,1,13*0,1,0,0,0
  //   ,1,5*0,1,0,1,9*0,1,0,1,5*0,1,5*0,1,0,0,0,1,5*0,1,5*0,1,0,1,9*0
  //   ,1,0,1,0,0,0,1,0,1,11*0,1,11*0,1,0,0,0,1,0,1,0,0,0,1,5*0,1,0,1
  //   ,9*0,1
  //   1 A
  //   2 B
  //   3 C
  //   4 D
  //   5 rRam
  //   6 nothing
  //   110011(LCM)
  //   101111(rotate right )
  //   Control Unit
  //   Memory
  //   001111(accA ← pRAM-adr[Operand])
  //   PC
  //   Jump
endmodule
